# Fritzing sketch ForceSensor (saved by Fritzing 0.9.5d)
breadboards: 1

parts:
  J1 = Basic Force Sensing Resistor (FSR) [package=THT]
  Part1 = Arduino Uno (Rev3)
  R1 = Resistor [tolerance=±5% resistance=10 package=THT]

nets:
  N1: J1.pin_0, Part1.5V, R1.Pin_0
  N2: J1.pin_1, Part1.A0, R1.Pin_1
